# Fritzing sketch SimpleSystemCircuit (saved by Fritzing 0.9.3b)
breadboards: 1

parts:
  R2 = Resistor [tolerance=±5% resistance=10k package=THT]
  On_Off_Switch = Toggle Switch [package=THT]
  Water_Switch = Toggle Switch [package=THT]
  4_Relay_Module = 4-Channel 5v Relay Shield [package=relay-4ch5v10a]
  R3 = Resistor [tolerance=±5% resistance=10k package=THT]
  L1 = Solenoid
  Part1 = Arduino Uno (Rev3)

nets:
  N1: R2.Pin_0, Water_Switch.L1, Part1.D3_PWM
  VCC: R2.Pin_1, 4_Relay_Module.VCC, R3.Pin_1, Part1.5V
  N2: On_Off_Switch.L1, R3.Pin_0, Part1.D7
  GND: On_Off_Switch.COM, Water_Switch.COM, 4_Relay_Module.GND, Part1.GND
  N3: 4_Relay_Module.IN4, Part1.A0
  N4: 4_Relay_Module.K4-Off, L1.pin1
  N5: 4_Relay_Module.K4-On, L1.pin2

notes:
  Water Switch
  On Off Switch
  Water Pump

custom parts:
  4-Channel 5v Relay Shield: 4 Channel 5v Relay Shield w. 2x SPD-06VDC-SD-C
