# Fritzing sketch Arduino_Pump_Control (saved by Fritzing 0.9.4)
breadboards: 1

parts:
  Part1 = Arduino Uno (Rev3)
  R2 = Resistor [tolerance=±5% resistance=10k package=THT]
  On_Off_Switch = Toggle Switch [package=THT]
  Water_Switch = Toggle Switch [package=THT]
  4_Relay_Module = 4-Channel 5v Relay Shield [package=relay-4ch5v10a]
  DS3231 = Adafruit DS3231 [part_number="Adafruit #3013"]
  dht22 = DHT22 module
  R3 = Resistor [tolerance=±5% resistance=10k package=THT]

nets:
  N1: Part1.A4/SDA, DS3231.SDA, DS3231.BAT
  N2: Part1.D8, 4_Relay_Module.IN4
  N3: Part1.D9_PWM, 4_Relay_Module.IN3
  N4: Part1.D10_PWM/SS, 4_Relay_Module.IN2
  GND: Part1.GND, R2.Pin_1, 4_Relay_Module.GND, 4_Relay_Module.IN1, DS3231.Vin, DS3231.GND, dht22.GND, R3.Pin_1
  N5: Part1.A5/SCL, DS3231.SCL
  N6: Part1.D3_PWM, R2.Pin_0, Water_Switch.L1
  N7: Part1.D6_PWM, dht22.VCC
  N8: Part1.D7, On_Off_Switch.L1, R3.Pin_0
  5V: Part1.5V, On_Off_Switch.COM, Water_Switch.COM, 4_Relay_Module.VCC, dht22.DATA

notes:
  Water Switch
  On Off Switch

custom parts:
  4-Channel 5v Relay Shield: 4 Channel 5v Relay Shield w. 2x SPD-06VDC-SD-C
  Adafruit DS3231: The datasheet for the DS3231 explains that this part is an "Extremely Accurate I²C-Integrated RTC/TCXO/Crystal". And, hey, it does exactly what it says on the tin! This Real Time Clock (RTC) is the most precise you can get in a small, low power package. Most RTCs use an external 32kHz timing crystal that is used to keep time with low current draw. And that's all well and good, but those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
